// Logisim project branch-comp.circ as structural Verilog: 1 circuit, main circuit branch_comp
module branch_comp (
  input  [31:0] BrData1,
  input  [31:0] BrData2,
  input  BrUn,
  output BrEq,
  output BrLt
);

  wire BrEq_Signed, BrEq_UnSigned, BrLess_Signed, BrLess_UnSigned;

  Comparator #(.width(32)) comparator_1 (.a(BrData1), .b(BrData2), .eq(BrEq_Signed), .lt(BrLess_Signed));  // open: gt
  Comparator #(.mode("unsigned"), .width(32)) comparator_2 (
    .a(BrData1), .b(BrData2), .eq(BrEq_UnSigned), .lt(BrLess_UnSigned));  // open: gt
  Multiplexer #(.enable("false")) multiplexer_1 (.in0(BrEq_Signed), .in1(BrEq_UnSigned), .out(BrEq), .sel(BrUn));
  Multiplexer #(.enable("false")) multiplexer_2 (.in0(BrLess_Signed), .in1(BrLess_UnSigned), .out(BrLt), .sel(BrUn));

  // Notes on the sheet:
  //   INPUTS to your circuit
  //   DON'T CHANGE THE LOCATIONS OF THE INPUTS AND OUTPUTS!
  //   OUTPUT from your circuit
endmodule
