// Logisim project control-logic.circ as structural Verilog: 1 circuit, main circuit control_logic
module control_logic (
  input  [31:0] Instruction,
  input  BrEq,
  input  BrLt,
  output PCSel,
  output RegWEn,
  output [2:0] ImmSel,
  output BrUn,
  output ASel,
  output BSel,
  output [3:0] ALUSel,
  output MemWEn,
  output [1:0] WBSel
);

  wire add, addi, and1, and_1_out, and_2_out, and_3_out, and_4_out, and_5_out, and_6_out, and_7_out,
       and_13_out, and_14_out, and_18_out, and_19_out, and_20_out, and_21_out, and_22_out, and_23_out,
       and_24_out, and_25_out, and_26_out, and_27_out, and_28_out, and_29_out, and_30_out, and_31_out,
       and_32_out, and_33_out, and_46_out, and_47_out, and_48_out, and_49_out, and_50_out, and_51_out,
       and_52_out, and_53_out, and_54_out, and_55_out, and_56_out, and_57_out, and_67_out, and_70_out,
       and_72_out, and_73_out, and_74_out, andi, auipc, B_type, beq, bge, bgeu, blt, bltu, bne,
       comparator_10_eq, comparator_11_eq, comparator_12_eq, comparator_13_eq, comparator_14_eq,
       comparator_15_eq, comparator_16_eq, comparator_17_eq, comparator_18_eq, comparator_19_eq,
       comparator_20_eq, comparator_21_eq, comparator_22_eq, comparator_23_eq, comparator_24_eq,
       comparator_25_eq, comparator_26_eq, comparator_27_eq, comparator_28_eq, comparator_29_eq,
       comparator_30_eq, comparator_31_eq, comparator_32_eq, comparator_33_eq, comparator_34_eq,
       comparator_35_eq, comparator_36_eq, comparator_37_eq, comparator_38_eq, comparator_39_eq,
       comparator_40_eq, comparator_41_eq, comparator_42_eq, comparator_43_eq, comparator_44_eq,
       comparator_45_eq, comparator_46_eq, comparator_47_eq, comparator_48_eq, comparator_49_eq,
       comparator_50_eq, comparator_51_eq, comparator_52_eq, I_type_imm, I_type_jalr, I_type_load, J_type,
       jal, jalr, lb, lh, lui, lw, mul, mulh, mulhu, not_1_out, not_2_out, or1, or_1_out, or_2_out, ori,
       priority_encoder_2_gs, R_type, S_type, sb, sh, sll1, slli, slt, slti, sra1, srai, srl1, srli, sub, sw,
       U_type_imm, U_type_pc, xor1, xori;
  wire [1:0] priority_encoder_2_out;
  wire [4:0] priority_encoder_1_out;
  wire [5:0] adder_1_out, bit_extender_1_out, bit_extender_2_out, ROMInput;
  wire [15:14] rom_1_data;

  Comparator #(.width(7)) comparator_1 (.a(Instruction[6:0]), .b(7'b0010011), .eq(I_type_imm));  // open: gt, lt
  Comparator #(.width(7)) comparator_2 (.a(Instruction[6:0]), .b(7'b0110011), .eq(R_type));  // open: gt, lt
  Comparator #(.width(7)) comparator_3 (.a(Instruction[6:0]), .b(7'b1100011), .eq(B_type));  // open: gt, lt
  Comparator #(.width(7)) comparator_4 (.a(Instruction[6:0]), .b(7'b1100111), .eq(I_type_jalr));  // open: gt, lt
  Comparator #(.width(7)) comparator_5 (.a(Instruction[6:0]), .b(7'b0000011), .eq(I_type_load));  // open: gt, lt
  Comparator #(.width(7)) comparator_6 (.a(Instruction[6:0]), .b(7'b0100011), .eq(S_type));  // open: gt, lt
  Comparator #(.width(7)) comparator_7 (.a(Instruction[6:0]), .b(7'b1101111), .eq(J_type));  // open: gt, lt
  Comparator #(.width(7)) comparator_8 (.a(Instruction[6:0]), .b(7'b0110111), .eq(U_type_imm));  // open: gt, lt
  Comparator #(.width(7)) comparator_9 (.a(Instruction[6:0]), .b(7'b0010111), .eq(U_type_pc));  // open: gt, lt
  ROM #(.addrWidth(6), .dataWidth(16)) rom_1 (
    .addr(ROMInput), .data({rom_1_data, WBSel, MemWEn, ALUSel, BSel, ASel, BrUn, ImmSel, RegWEn}));
  and and_1 (and_1_out, I_type_imm, 1'b1);
  Comparator #(.width(3)) comparator_10 (.a(Instruction[14:12]), .b(3'b000), .eq(comparator_10_eq));  // open: gt, lt
  and and_2 (and_2_out, I_type_imm, 1'b1);
  Comparator #(.width(3)) comparator_11 (.a(Instruction[14:12]), .b(3'b111), .eq(comparator_11_eq));  // open: gt, lt
  and and_3 (and_3_out, I_type_imm, 1'b1);
  Comparator #(.width(3)) comparator_12 (.a(Instruction[14:12]), .b(3'b110), .eq(comparator_12_eq));  // open: gt, lt
  and and_4 (and_4_out, I_type_imm, 1'b1);
  Comparator #(.width(3)) comparator_13 (.a(Instruction[14:12]), .b(3'b100), .eq(comparator_13_eq));  // open: gt, lt
  and and_5 (and_5_out, I_type_imm, 1'b1);
  Comparator #(.width(3)) comparator_14 (.a(Instruction[14:12]), .b(3'b010), .eq(comparator_14_eq));  // open: gt, lt
  and and_6 (and_6_out, I_type_imm, 1'b1);
  Comparator #(.width(3)) comparator_15 (.a(Instruction[14:12]), .b(3'b001), .eq(comparator_15_eq));  // open: gt, lt
  and and_7 (and_7_out, I_type_imm, 1'b1);
  Comparator #(.width(3)) comparator_16 (.a(Instruction[14:12]), .b(3'b101), .eq(comparator_16_eq));  // open: gt, lt
  and and_8 (addi, and_1_out, comparator_10_eq);
  and and_9 (andi, and_2_out, comparator_11_eq);
  and and_10 (ori, and_3_out, comparator_12_eq);
  and and_11 (xori, and_4_out, comparator_13_eq);
  and and_12 (slti, and_5_out, comparator_14_eq);
  and and_13 (and_13_out, and_6_out, comparator_15_eq);
  and and_14 (and_14_out, and_7_out, comparator_16_eq);
  Comparator #(.width(7)) comparator_17 (.a(Instruction[31:25]), .b({7{1'b0}}), .eq(comparator_17_eq));  // open: gt, lt
  and and_15 (slli, and_13_out, comparator_17_eq);
  Comparator #(.width(7)) comparator_18 (.a(Instruction[31:25]), .b({7{1'b0}}), .eq(comparator_18_eq));  // open: gt, lt
  Comparator #(.width(7)) comparator_19 (
    .a(Instruction[31:25]), .b(7'b0100000), .eq(comparator_19_eq));  // open: gt, lt
  and and_16 (srli, and_14_out, comparator_18_eq);
  and and_17 (srai, and_14_out, comparator_19_eq);
  Priority_Encoder #(.select(5)) priority_encoder_1 (
    .in0(add), .in1(mul), .in2(sub), .in3(sll1), .in4(mulh), .in5(mulhu), .in6(slt), .in7(xor1), .in8(srl1),
    .in9(sra1), .in10(or1), .in11(and1), .in12(lb), .in13(lh), .in14(lw), .in15(addi), .in16(slli),
    .in17(slti), .in18(xori), .in19(srli), .in20(srai), .in21(ori), .in22(andi), .in23(sb), .in24(sh),
    .in25(sw), .in26(beq), .in27(bne), .in28(blt), .in29(bge), .in30(bltu), .in31(bgeu),
    .out(priority_encoder_1_out));  // open: gs, en_out, en_in
  Priority_Encoder #(.select(2)) priority_encoder_2 (
    .in0(auipc), .in1(lui), .in2(jal), .in3(jalr), .out(priority_encoder_2_out), .gs(priority_encoder_2_gs));  // open: en_out, en_in
  and and_18 (and_18_out, R_type, 1'b1);
  Comparator #(.width(3)) comparator_20 (.a(Instruction[14:12]), .b(3'b000), .eq(comparator_20_eq));  // open: gt, lt
  and and_19 (and_19_out, R_type, 1'b1);
  Comparator #(.width(3)) comparator_21 (.a(Instruction[14:12]), .b(3'b001), .eq(comparator_21_eq));  // open: gt, lt
  and and_20 (and_20_out, R_type, 1'b1);
  Comparator #(.width(3)) comparator_22 (.a(Instruction[14:12]), .b(3'b010), .eq(comparator_22_eq));  // open: gt, lt
  and and_21 (and_21_out, R_type, 1'b1);
  Comparator #(.width(3)) comparator_23 (.a(Instruction[14:12]), .b(3'b011), .eq(comparator_23_eq));  // open: gt, lt
  and and_22 (and_22_out, R_type, 1'b1);
  Comparator #(.width(3)) comparator_24 (.a(Instruction[14:12]), .b(3'b100), .eq(comparator_24_eq));  // open: gt, lt
  and and_23 (and_23_out, R_type, 1'b1);
  Comparator #(.width(3)) comparator_25 (.a(Instruction[14:12]), .b(3'b101), .eq(comparator_25_eq));  // open: gt, lt
  and and_24 (and_24_out, R_type, 1'b1);
  Comparator #(.width(3)) comparator_26 (.a(Instruction[14:12]), .b(3'b110), .eq(comparator_26_eq));  // open: gt, lt
  and and_25 (and_25_out, R_type, 1'b1);
  Comparator #(.width(3)) comparator_27 (.a(Instruction[14:12]), .b(3'b111), .eq(comparator_27_eq));  // open: gt, lt
  and and_26 (and_26_out, and_18_out, comparator_20_eq);
  and and_27 (and_27_out, and_19_out, comparator_21_eq);
  and and_28 (and_28_out, and_20_out, comparator_22_eq);
  and and_29 (and_29_out, and_21_out, comparator_23_eq);
  and and_30 (and_30_out, and_22_out, comparator_24_eq);
  and and_31 (and_31_out, and_23_out, comparator_25_eq);
  and and_32 (and_32_out, and_24_out, comparator_26_eq);
  and and_33 (and_33_out, and_25_out, comparator_27_eq);
  assign bit_extender_1_out = {{1{1'b0}}, priority_encoder_1_out};  // Bit_Extender bit_extender_1
  assign bit_extender_2_out = {{4{1'b0}}, priority_encoder_2_out};  // Bit_Extender bit_extender_2
  Adder #(.width(6)) adder_1 (.a(bit_extender_2_out), .b(6'b100000), .out(adder_1_out));  // open: cin, cout
  Comparator #(.width(7)) comparator_28 (.a(Instruction[31:25]), .b({7{1'b0}}), .eq(comparator_28_eq));  // open: gt, lt
  Comparator #(.width(7)) comparator_29 (
    .a(Instruction[31:25]), .b(7'b0100000), .eq(comparator_29_eq));  // open: gt, lt
  Comparator #(.width(7)) comparator_30 (
    .a(Instruction[31:25]), .b(7'b0000001), .eq(comparator_30_eq));  // open: gt, lt
  Comparator #(.width(7)) comparator_31 (.a(Instruction[31:25]), .b({7{1'b0}}), .eq(comparator_31_eq));  // open: gt, lt
  Comparator #(.width(7)) comparator_32 (
    .a(Instruction[31:25]), .b(7'b0000001), .eq(comparator_32_eq));  // open: gt, lt
  Comparator #(.width(7)) comparator_33 (.a(Instruction[31:25]), .b({7{1'b0}}), .eq(comparator_33_eq));  // open: gt, lt
  Comparator #(.width(7)) comparator_34 (
    .a(Instruction[31:25]), .b(7'b0000001), .eq(comparator_34_eq));  // open: gt, lt
  Comparator #(.width(7)) comparator_35 (.a(Instruction[31:25]), .b({7{1'b0}}), .eq(comparator_35_eq));  // open: gt, lt
  Comparator #(.width(7)) comparator_36 (.a(Instruction[31:25]), .b({7{1'b0}}), .eq(comparator_36_eq));  // open: gt, lt
  Comparator #(.width(7)) comparator_37 (
    .a(Instruction[31:25]), .b(7'b0100000), .eq(comparator_37_eq));  // open: gt, lt
  Comparator #(.width(7)) comparator_38 (.a(Instruction[31:25]), .b({7{1'b0}}), .eq(comparator_38_eq));  // open: gt, lt
  Comparator #(.width(7)) comparator_39 (.a(Instruction[31:25]), .b({7{1'b0}}), .eq(comparator_39_eq));  // open: gt, lt
  and and_34 (add, and_26_out, comparator_28_eq);
  and and_35 (sub, and_26_out, comparator_29_eq);
  and and_36 (mul, and_26_out, comparator_30_eq);
  and and_37 (sll1, and_27_out, comparator_31_eq);
  and and_38 (mulh, and_27_out, comparator_32_eq);
  and and_39 (slt, and_28_out, comparator_33_eq);
  and and_40 (mulhu, and_29_out, comparator_34_eq);
  and and_41 (xor1, and_30_out, comparator_35_eq);
  and and_42 (srl1, and_31_out, comparator_36_eq);
  and and_43 (sra1, and_31_out, comparator_37_eq);
  and and_44 (or1, and_32_out, comparator_38_eq);
  and and_45 (and1, and_33_out, comparator_39_eq);
  or or_1 (or_1_out, blt, bltu);
  Multiplexer #(.enable("false"), .width(6)) multiplexer_1 (
    .in0(bit_extender_1_out), .in1(adder_1_out), .out(ROMInput), .sel(priority_encoder_2_gs));
  not not_1 (not_1_out, BrLt);
  or or_2 (or_2_out, bge, bgeu);
  and and_46 (and_46_out, BrEq, beq);
  and and_47 (and_47_out, not_1_out, or_2_out);
  and and_48 (and_48_out, BrLt, or_1_out);
  and and_49 (and_49_out, B_type, 1'b1);
  Comparator #(.width(3)) comparator_40 (.a(Instruction[14:12]), .b(3'b000), .eq(comparator_40_eq));  // open: gt, lt
  and and_50 (and_50_out, B_type, 1'b1);
  Comparator #(.width(3)) comparator_41 (.a(Instruction[14:12]), .b(3'b101), .eq(comparator_41_eq));  // open: gt, lt
  and and_51 (and_51_out, B_type, 1'b1);
  Comparator #(.width(3)) comparator_42 (.a(Instruction[14:12]), .b(3'b111), .eq(comparator_42_eq));  // open: gt, lt
  and and_52 (and_52_out, B_type, 1'b1);
  Comparator #(.width(3)) comparator_43 (.a(Instruction[14:12]), .b(3'b100), .eq(comparator_43_eq));  // open: gt, lt
  and and_53 (and_53_out, B_type, 1'b1);
  Comparator #(.width(3)) comparator_44 (.a(Instruction[14:12]), .b(3'b110), .eq(comparator_44_eq));  // open: gt, lt
  and and_54 (and_54_out, B_type, 1'b1);
  Comparator #(.width(3)) comparator_45 (.a(Instruction[14:12]), .b(3'b001), .eq(comparator_45_eq));  // open: gt, lt
  and and_55 (and_55_out, I_type_load, 1'b1);
  Comparator #(.width(3)) comparator_46 (.a(Instruction[14:12]), .b(3'b000), .eq(comparator_46_eq));  // open: gt, lt
  and and_56 (and_56_out, I_type_load, 1'b1);
  Comparator #(.width(3)) comparator_47 (.a(Instruction[14:12]), .b(3'b001), .eq(comparator_47_eq));  // open: gt, lt
  and and_57 (and_57_out, I_type_load, 1'b1);
  Comparator #(.width(3)) comparator_48 (.a(Instruction[14:12]), .b(3'b010), .eq(comparator_48_eq));  // open: gt, lt
  not not_2 (not_2_out, BrEq);
  and and_58 (beq, and_49_out, comparator_40_eq);
  and and_59 (bge, and_50_out, comparator_41_eq);
  and and_60 (bgeu, and_51_out, comparator_42_eq);
  and and_61 (blt, and_52_out, comparator_43_eq);
  and and_62 (bltu, and_53_out, comparator_44_eq);
  and and_63 (bne, and_54_out, comparator_45_eq);
  and and_64 (lb, and_55_out, comparator_46_eq);
  and and_65 (lh, and_56_out, comparator_47_eq);
  and and_66 (lw, and_57_out, comparator_48_eq);
  and and_67 (and_67_out, bne, not_2_out);
  // OR_Gate or_3 has open pins: in0=and_47_out, in1=jal, in2=and_46_out, in3=and_48_out, in4=jalr, in5=and_67_out, out=open
  Comparator #(.width(3)) comparator_49 (.a(Instruction[14:12]), .b(3'b000), .eq(comparator_49_eq));  // open: gt, lt
  and and_68 (lui, U_type_imm, 1'b1);
  and and_69 (auipc, U_type_pc, 1'b1);
  and and_70 (and_70_out, I_type_jalr, 1'b1);
  and and_71 (jalr, and_70_out, comparator_49_eq);
  and and_72 (and_72_out, S_type, 1'b1);
  Comparator #(.width(3)) comparator_50 (.a(Instruction[14:12]), .b(3'b000), .eq(comparator_50_eq));  // open: gt, lt
  and and_73 (and_73_out, S_type, 1'b1);
  Comparator #(.width(3)) comparator_51 (.a(Instruction[14:12]), .b(3'b001), .eq(comparator_51_eq));  // open: gt, lt
  and and_74 (and_74_out, S_type, 1'b1);
  Comparator #(.width(3)) comparator_52 (.a(Instruction[14:12]), .b(3'b010), .eq(comparator_52_eq));  // open: gt, lt
  and and_75 (sb, and_72_out, comparator_50_eq);
  and and_76 (sh, and_73_out, comparator_51_eq);
  and and_77 (sw, and_74_out, comparator_52_eq);
  and and_78 (jal, J_type, 1'b1);

  // Other names for the same wires on the sheet: Opcode[6:0] = Instruction[6:0]; rd[4:0] = Instruction[11:7];
  //   funct3[2:0] = Instruction[14:12]; funct7[6:0] = Instruction[31:25]

  // Notes on the sheet:
  //   INPUTS to your circuit
  //   Connect ROM Input here ->
  //   contents of rom_1 (hex, n*v repeats v):
  //   1001 1401 1601 1081 1481 1581 1101 1201 1281 1681 1301 1381 41 41 41 1041 10c1 1141 1241 12c1 16c1
  //   1341 13c1 842 842 842 4*64 74 74 1067 17c7 2069 2041
  //   ROM FOR CONTROL LOGIC
  //   DON'T CHANGE THE LOCATIONS OF THE INPUTS AND OUTPUTS!
  //   This is only if you choose to do the ROM option
  //   CONNECT
  //   WIRE
  //   TO
  //   USE
  //   ROM
  //   OUTPUT from your circuit
endmodule
