// Logisim project cpu.circ as structural Verilog: 1 circuit, main circuit cpu
module cpu (
  input  clk,
  input  [31:0] Instruction,
  input  [31:0] MemReadData,
  output [31:0] MemAddress,
  output [31:0] ProgramCounter,
  output [31:0] ra,
  output [31:0] sp,
  output [31:0] t0,
  output [31:0] t1,
  output [31:0] t2,
  output [31:0] s0,
  output [31:0] s1,
  output [31:0] a0,
  output [3:0] MemWriteMask,
  output [31:0] MemWriteData
);

  wire ASel, BrEq, BrLt, BrUn, BSel, MemWEn, PCSel, RegWEn;
  wire [1:0] WBSel;
  wire [2:0] Funct3, ImmSel;
  wire [3:0] ALUSel;
  wire [6:0] Funct7;
  wire [24:0] Inst;
  wire [31:0] adder_1_out, adder_2_out, aluA, aluB, Imm, multiplexer_1_out, multiplexer_2_out,
       partial_load_1_datatoreg, pc, rd1, rd2, wb;

  Adder #(.width(32)) adder_1 (.a(ProgramCounter), .b(32'h4), .out(adder_1_out));  // open: cin, cout
  Register #(.width(32)) u_PC (.D(multiplexer_1_out), .clk(clk), .Q(ProgramCounter));  // open: en, clr
  Multiplexer #(.enable("false"), .width(32)) multiplexer_1 (
    .in0(adder_1_out), .in1(MemAddress), .out(multiplexer_1_out), .sel(PCSel));
  Register #(.width(32)) register_1 (.D(ProgramCounter), .clk(clk), .Q(pc));  // open: en, clr
  control_logic control_logic_1 (
    .PCSel(PCSel), .RegWEn(RegWEn), .ImmSel(ImmSel), .BrUn(BrUn), .ASel(ASel), .BSel(BSel), .ALUSel(ALUSel),
    .MemWEn(MemWEn), .WBSel(WBSel), .Instruction({Funct7, Inst[24:15], Funct3, Inst[11:0]}), .BrEq(BrEq),
    .BrLt(BrLt));
  regfile regfile_1 (
    .ReadReg1(Inst[19:15]), .ReadReg2(Inst[24:20]), .WriteReg(Inst[11:7]), .RegWriteData(wb),
    .RegWEn(RegWEn), .clk(clk), .ra(ra), .sp(sp), .t0(t0), .t1(t1), .t2(t2), .s0(s0), .s1(s1), .a0(a0),
    .RegReadData1(rd1), .RegReadData2(rd2));
  imm_gen imm_gen_1 (.Instruction({Funct7, Inst[24:15], Funct3, Inst[11:0]}), .ImmSel(ImmSel), .Immediate(Imm));
  Register #(.width(32)) register_2 (
    .D(multiplexer_2_out), .clk(clk), .Q({Funct7, Inst[24:15], Funct3, Inst[11:0]}));  // open: en, clr
  Multiplexer #(.enable("false"), .width(32)) multiplexer_2 (
    .in0(Instruction), .in1(32'h13), .out(multiplexer_2_out), .sel(PCSel));
  Multiplexer #(.enable("false"), .width(32)) multiplexer_3 (.in0(rd1), .in1(pc), .out(aluA), .sel(ASel));
  Multiplexer #(.enable("false"), .width(32)) multiplexer_4 (.in0(rd2), .in1(Imm), .out(aluB), .sel(BSel));
  branch_comp branch_comp_1 (.BrData1(rd1), .BrData2(rd2), .BrUn(BrUn), .BrEq(BrEq), .BrLt(BrLt));
  alu alu_1 (.ALUResult(MemAddress), .A(aluA), .B(aluB), .ALUSel(ALUSel));
  partial_store partial_store_1 (
    .Instruction({Funct7, Inst[24:15], Funct3, Inst[11:0]}), .MemAddress(MemAddress), .DataFromReg(rd2),
    .MemWEn(MemWEn), .MemWriteMask(MemWriteMask), .DataToMem(MemWriteData));
  partial_load partial_load_1 (
    .Instruction({Funct7, Inst[24:15], Funct3, Inst[11:0]}), .MemAddress(MemAddress),
    .DataFromMem(MemReadData), .DataToReg(partial_load_1_datatoreg));
  Adder #(.width(32)) adder_2 (.a(pc), .b(32'h4), .out(adder_2_out));  // open: cin, cout
  Multiplexer #(.enable("false"), .select(2), .width(32)) multiplexer_5 (
    .in0(partial_load_1_datatoreg), .in1(MemAddress), .in2(adder_2_out), .out(wb), .sel(WBSel));  // open: in3

  // Other names for the same wires on the sheet: ALUResult[31:0] = MemAddress; Opcode[6:0] = Inst[6:0];
  //   rd[4:0] = Inst[11:7]; Inst (some bits) = {Funct7, Funct3}; rs1[4:0] = Inst[19:15]; rs2[4:0] = Inst[24:20]

  // Notes on the sheet:
  //   To IMEM
  //   IMEM (do **NOT** move this)
  //   From IMEM
  //   Inputs/Outputs for testing. Do **NOT** move these.
  //   It is OK to move the PC, RegFile, ALU, MEM, Branch Comp, Imm Gen, Partial Load, Partial Store and Control Logic to wherever is most convenient for you when constructing your CPU, and to delete this text
  //   To DMEM
  //   DMEM (do **NOT** move this)
  //   From DMEM
endmodule
