// Logisim project imm-gen.circ as structural Verilog: 1 circuit, main circuit imm_gen
module imm_gen (
  input  [31:0] Instruction,
  input  [2:0] ImmSel,
  output [31:0] Immediate
);

  wire [31:0] B_Type, I_Type, J_Type, S_Type;

  assign I_Type = {{20{Instruction[31]}}, Instruction[31:20]};  // Bit_Extender bit_extender_1
  assign S_Type = {{20{Instruction[31]}}, {Instruction[31:25], Instruction[11:7]}};  // Bit_Extender bit_extender_2
  assign B_Type = {{19{Instruction[31]}}, {Instruction[31], Instruction[7], Instruction[30:25], Instruction[11:8], 1'b0}};  // Bit_Extender bit_extender_3
  assign J_Type = {{11{Instruction[31]}}, {Instruction[31], Instruction[19:12], Instruction[20], Instruction[30:21], 1'b0}};  // Bit_Extender bit_extender_4
  Multiplexer #(.enable("false"), .select(3), .width(32)) multiplexer_1 (
    .in0(I_Type), .in1(S_Type), .in2(B_Type), .in3({Instruction[31:12], {12{1'b0}}}), .in4(J_Type),
    .in5(J_Type), .in6(J_Type), .in7(J_Type), .out(Immediate), .sel(ImmSel));

  // Other names for the same wires on the sheet: Bit_20 = Instruction[20]; U_Type[31:12] = Instruction[31:12];
  //   Bit_21 = Instruction[21]; Bit_22 = Instruction[22]; Bit_23 = Instruction[23]; Bit_24 = Instruction[24];
  //   Bit_7 = Instruction[7]; Bit_8 = Instruction[8]; Bit_9 = Instruction[9]; Bit_10 = Instruction[10];
  //   Bit_11 = Instruction[11]; Bit_25 = Instruction[25]; Bit_26 = Instruction[26]; Bit_27 = Instruction[27];
  //   Bit_28 = Instruction[28]; Bit_29 = Instruction[29]; Bit_30 = Instruction[30]; Bit_31 = Instruction[31];
  //   Bit_0 = Instruction[0]; Bit_1 = Instruction[1]; Bit_2 = Instruction[2]; Bit_3 = Instruction[3];
  //   Bit_4 = Instruction[4]; Bit_5 = Instruction[5]; Bit_6 = Instruction[6]; Bit_12 = Instruction[12];
  //   Bit_13 = Instruction[13]; Bit_14 = Instruction[14]; Bit_15 = Instruction[15]; Bit_16 = Instruction[16];
  //   Bit_17 = Instruction[17]; Bit_18 = Instruction[18]; Bit_19 = Instruction[19]

  // Notes on the sheet:
  //   INPUTS to your circuit
  //   DON'T CHANGE THE LOCATIONS OF THE INPUTS AND OUTPUTS!
  //   OUTPUT from your circuit
endmodule
