// Logisim project partial-store.circ as structural Verilog: 1 circuit, main circuit partial_store
module partial_store (
  input  [31:0] Instruction,
  input  [31:0] MemAddress,
  input  [31:0] DataFromReg,
  input  MemWEn,
  output [3:0] MemWriteMask,
  output [31:0] DataToMem
);

  wire comparator_1_eq;
  wire [3:0] multiplexer_1_out, multiplexer_2_out, multiplexer_3_out;
  wire [31:0] multiplexer_4_out, multiplexer_5_out;

  Multiplexer #(.enable("false"), .select(2), .width(4)) multiplexer_1 (
    .in0(4'b0001), .in1(4'b0010), .in2(4'b0100), .in3(4'b1000), .out(multiplexer_1_out), .sel(MemAddress[1:0]));
  Multiplexer #(.enable("false"), .select(2), .width(4)) multiplexer_2 (
    .in0(4'b0011), .in1(4'b0011), .in2(4'b1100), .in3(4'b1100), .out(multiplexer_2_out), .sel(MemAddress[1:0]));
  Multiplexer #(.enable("false"), .select(3), .width(4)) multiplexer_3 (
    .in0(multiplexer_1_out), .in1(multiplexer_2_out), .in2(4'b1111), .in3(4'b1111), .in4(4'b1111),
    .in5(4'b1111), .in6(4'b1111), .in7(4'b1111), .out(multiplexer_3_out), .sel(Instruction[14:12]));
  Comparator #(.width(7)) comparator_1 (.a(7'b0100011), .b(Instruction[6:0]), .eq(comparator_1_eq));  // open: gt, lt
  Multiplexer #(.enable("false"), .select(2), .width(32)) multiplexer_4 (
    .in0({{24{1'b0}}, DataFromReg[7:0]}), .in1({{16{1'b0}}, DataFromReg[7:0], {8{1'b0}}}),
    .in2({{8{1'b0}}, DataFromReg[7:0], {16{1'b0}}}), .in3({DataFromReg[7:0], {24{1'b0}}}),
    .out(multiplexer_4_out), .sel(MemAddress[1:0]));
  Multiplexer #(.enable("false"), .select(2), .width(32)) multiplexer_5 (
    .in0({{16{1'b0}}, DataFromReg[15:0]}), .in1({{16{1'b0}}, DataFromReg[15:0]}),
    .in2({DataFromReg[15:0], {16{1'b0}}}), .in3({DataFromReg[15:0], {16{1'b0}}}), .out(multiplexer_5_out),
    .sel(MemAddress[1:0]));
  Multiplexer #(.enable("false"), .width(4)) multiplexer_6 (
    .in0(4'b0000), .in1(multiplexer_3_out), .out(MemWriteMask), .sel(comparator_1_eq));
  Multiplexer #(.enable("false"), .select(3), .width(32)) multiplexer_7 (
    .in0(multiplexer_4_out), .in1(multiplexer_5_out), .in2(DataFromReg), .in3(DataFromReg),
    .in4(DataFromReg), .in5(DataFromReg), .in6(DataFromReg), .in7(DataFromReg), .out(DataToMem),
    .sel(Instruction[14:12]));

  // Other names for the same wires on the sheet: Data7_0[7:0] = DataFromReg[7:0]; Data15_0[15:0] = DataFromReg[15:0];
  //   Opcode[6:0] = Instruction[6:0]; Funct3[2:0] = Instruction[14:12]; Bottom2[1:0] = MemAddress[1:0]

  // Notes on the sheet:
  //   INPUTS to your circuit
  //   DON'T CHANGE THE LOCATIONS OF THE INPUTS AND OUTPUTS!
  //   OUTPUT from your circuit
endmodule
