// Logisim project regfile.circ as structural Verilog: 1 circuit, main circuit regfile
module regfile (
  input  [4:0] ReadReg1,
  input  [4:0] ReadReg2,
  input  [4:0] WriteReg,
  input  [31:0] RegWriteData,
  input  RegWEn,
  input  clk,
  output [31:0] ra,
  output [31:0] sp,
  output [31:0] t0,
  output [31:0] t1,
  output [31:0] t2,
  output [31:0] s0,
  output [31:0] s1,
  output [31:0] a0,
  output [31:0] RegReadData1,
  output [31:0] RegReadData2
);

  wire a0c, a1c, a2c, a3c, a4c, a5c, a6c, a7c, gpc, rac, s0c, s1c, s2c, s3c, s4c, s5c, s6c, s7c, s8c, s9c,
       s10c, s11c, spc, t0c, t1c, t2c, t3c, t4c, t5c, t6c, tpc;
  wire [31:0] a1, a2, a3, a4, a5, a6, a7, gp, s2, s3, s4, s5, s6, s7, s8, s9, s10, s11, t3, t4, t5, t6, tp,
       zero;

  Demultiplexer #(.enable("false"), .select(5)) demultiplexer_1 (
    .out1(rac), .out2(spc), .out3(gpc), .out4(tpc), .out5(t0c), .out6(t1c), .out7(t2c), .out8(s0c),
    .out9(s1c), .out10(a0c), .out11(a1c), .out12(a2c), .out13(a3c), .out14(a4c), .out15(a5c), .out16(a6c),
    .out17(a7c), .out18(s2c), .out19(s3c), .out20(s4c), .out21(s5c), .out22(s6c), .out23(s7c), .out24(s8c),
    .out25(s9c), .out26(s10c), .out27(s11c), .out28(t3c), .out29(t4c), .out30(t5c), .out31(t6c), .in(RegWEn),
    .sel(WriteReg));  // open: out0
  Register #(.width(32)) register_1 (.D({32{1'b0}}), .en(1'b1), .clk(clk), .Q(zero));  // open: clr
  Register #(.width(32)) register_2 (.D(RegWriteData), .en(rac), .clk(clk), .Q(ra));  // open: clr
  Register #(.width(32)) register_3 (.D(RegWriteData), .en(spc), .clk(clk), .Q(sp));  // open: clr
  Register #(.width(32)) register_4 (.D(RegWriteData), .en(gpc), .clk(clk), .Q(gp));  // open: clr
  Register #(.width(32)) register_5 (.D(RegWriteData), .en(tpc), .clk(clk), .Q(tp));  // open: clr
  Register #(.width(32)) register_6 (.D(RegWriteData), .en(t0c), .clk(clk), .Q(t0));  // open: clr
  Register #(.width(32)) register_7 (.D(RegWriteData), .en(t1c), .clk(clk), .Q(t1));  // open: clr
  Register #(.width(32)) register_8 (.D(RegWriteData), .en(t2c), .clk(clk), .Q(t2));  // open: clr
  Register #(.width(32)) register_9 (.D(RegWriteData), .en(s0c), .clk(clk), .Q(s0));  // open: clr
  Register #(.width(32)) register_10 (.D(RegWriteData), .en(s1c), .clk(clk), .Q(s1));  // open: clr
  Register #(.width(32)) register_11 (.D(RegWriteData), .en(a0c), .clk(clk), .Q(a0));  // open: clr
  Register #(.width(32)) register_12 (.D(RegWriteData), .en(a1c), .clk(clk), .Q(a1));  // open: clr
  Register #(.width(32)) register_13 (.D(RegWriteData), .en(a2c), .clk(clk), .Q(a2));  // open: clr
  Register #(.width(32)) register_14 (.D(RegWriteData), .en(a3c), .clk(clk), .Q(a3));  // open: clr
  Register #(.width(32)) register_15 (.D(RegWriteData), .en(a4c), .clk(clk), .Q(a4));  // open: clr
  Register #(.width(32)) register_16 (.D(RegWriteData), .en(t2c), .clk(clk), .Q(a5));  // open: clr
  Register #(.width(32)) register_17 (.D(RegWriteData), .en(a6c), .clk(clk), .Q(a6));  // open: clr
  Register #(.width(32)) register_18 (.D(RegWriteData), .en(a7c), .clk(clk), .Q(a7));  // open: clr
  Register #(.width(32)) register_19 (.D(RegWriteData), .en(s2c), .clk(clk), .Q(s2));  // open: clr
  Register #(.width(32)) register_20 (.D(RegWriteData), .en(s3c), .clk(clk), .Q(s3));  // open: clr
  Register #(.width(32)) register_21 (.D(RegWriteData), .en(s4c), .clk(clk), .Q(s4));  // open: clr
  Register #(.width(32)) register_22 (.D(RegWriteData), .en(s5c), .clk(clk), .Q(s5));  // open: clr
  Register #(.width(32)) register_23 (.D(RegWriteData), .en(s6c), .clk(clk), .Q(s6));  // open: clr
  Register #(.width(32)) register_24 (.D(RegWriteData), .en(s7c), .clk(clk), .Q(s7));  // open: clr
  Register #(.width(32)) register_25 (.D(RegWriteData), .en(s8c), .clk(clk), .Q(s8));  // open: clr
  Register #(.width(32)) register_26 (.D(RegWriteData), .en(s9c), .clk(clk), .Q(s9));  // open: clr
  Register #(.width(32)) register_27 (.D(RegWriteData), .en(s10c), .clk(clk), .Q(s10));  // open: clr
  Register #(.width(32)) register_28 (.D(RegWriteData), .en(s11c), .clk(clk), .Q(s11));  // open: clr
  Register #(.width(32)) register_29 (.D(RegWriteData), .en(t3c), .clk(clk), .Q(t3));  // open: clr
  Register #(.width(32)) register_30 (.D(RegWriteData), .en(t4c), .clk(clk), .Q(t4));  // open: clr
  Register #(.width(32)) register_31 (.D(RegWriteData), .en(t5c), .clk(clk), .Q(t5));  // open: clr
  Register #(.width(32)) register_32 (.D(RegWriteData), .en(t6c), .clk(clk), .Q(t6));  // open: clr
  Multiplexer #(.enable("false"), .select(5), .width(32)) multiplexer_1 (
    .in0(zero), .in1(ra), .in2(sp), .in3(gp), .in4(tp), .in5(t0), .in6(t1), .in7(t2), .in8(s0), .in9(s1),
    .in10(a0), .in11(a1), .in12(a2), .in13(a3), .in14(a4), .in15(a5), .in16(a6), .in17(a7), .in18(s2),
    .in19(s3), .in20(s4), .in21(s5), .in22(s6), .in23(s7), .in24(s8), .in25(s9), .in26(s10), .in27(s11),
    .in28(t3), .in29(t4), .in30(t5), .in31(t6), .out(RegReadData1), .sel(ReadReg1));
  Multiplexer #(.enable("false"), .select(5), .width(32)) multiplexer_2 (
    .in0(zero), .in1(ra), .in2(sp), .in3(gp), .in4(tp), .in5(t0), .in6(t1), .in7(t2), .in8(s0), .in9(s1),
    .in10(a0), .in11(a1), .in12(a2), .in13(a3), .in14(a4), .in15(a5), .in16(a6), .in17(a7), .in18(s2),
    .in19(s3), .in20(s4), .in21(s5), .in22(s6), .in23(s7), .in24(s8), .in25(s9), .in26(s10), .in27(s11),
    .in28(t3), .in29(t4), .in30(t5), .in31(t6), .out(RegReadData2), .sel(ReadReg2));

  // Notes on the sheet:
  //   INPUTS to your circuit
  //   DON'T CHANGE THE LOCATIONS OF THE INPUTS AND OUTPUTS!
  //   These are DEBUG/TEST outputs from your circuit.
  //   OUTPUTS from your circuit
endmodule
